# Fritzing sketch clock_back_pcb (saved by Fritzing 0.9.4)
circuit board: 3.9cm x 7cm
perfboards: 1

parts:
  Arduino_Nano_v3 = Arduino Nano (Rev3.0)
  J3 = male pin header, 4 pins [form="♂ (male)"]
  J4 = male pin header, 4 pins [form="♂ (male)"]
  J5 = male pin header, 7 pins [form="♂ (male)"]
  J7 = male pin header, 3 pins [form="♂ (male)"]
  J8 = shrouded pin header, 16 pins [form="♂ (shrouded male)"]
  C1 = Ceramic Capacitor [capacitance=100nF package="100 mil [THT, multilayer]"]
  J9 = male pin header, 2 pins [form="♂ (male)"]

nets:
  N1: Arduino_Nano_v3.GND, J5.pin6, J8.pin2, J8.pin3, J8.pin4, J8.pin13, J8.pin14, J8.pin15, C1.0, J9.pin2
  N2: Arduino_Nano_v3.D3, J5.pin7
  N3: Arduino_Nano_v3.D4, J5.pin5
  N4: Arduino_Nano_v3.D5, J5.pin4
  N5: Arduino_Nano_v3.D6, J7.pin1
  N6: Arduino_Nano_v3.D7, J7.pin2
  N7: Arduino_Nano_v3.D8, J7.pin3
  N8: Arduino_Nano_v3.D9, J3.pin1
  N9: Arduino_Nano_v3.D10, J3.pin2
  N10: Arduino_Nano_v3.D11/MOSI, J3.pin3
  N11: Arduino_Nano_v3.D12/MISO, J3.pin4
  N12: Arduino_Nano_v3.5V, J5.pin3, J8.pin6, J8.pin11, C1.1, J9.pin1
  N13: Arduino_Nano_v3.A5, J5.pin2
  N14: Arduino_Nano_v3.A4, J5.pin1
  N15: Arduino_Nano_v3.A3, J4.pin1
  N16: Arduino_Nano_v3.A2, J4.pin2
  N17: Arduino_Nano_v3.A1, J4.pin3
  N18: Arduino_Nano_v3.A0, J4.pin4

notes:
  -12v
  toggle
  paused
  tap
  +5v
  GND
