# Fritzing sketch clock_front_pcb (saved by Fritzing 0.9.4)
circuit board: 4cm x 10cm
perfboards: 1

parts:
  R1 = Resistor [tolerance=±5% resistance=220 package=THT]
  R2 = Resistor [tolerance=±5% resistance=220 package=THT]
  LED2 = LED - 5mm [color="Red (633nm)" package="5 mm [THT]"]
  R3 = Resistor [tolerance=±5% resistance=220 package=THT]
  R4 = Resistor [tolerance=±5% resistance=220 package=THT]
  LED3 = LED - 5mm [color="Red (633nm)" package="5 mm [THT]"]
  R5 = Resistor [tolerance=±5% resistance=220 package=THT]
  R6 = Resistor [tolerance=±5% resistance=220 package=THT]
  R7 = Resistor [tolerance=±5% resistance=220 package=THT]
  R8 = Resistor [tolerance=±5% resistance=220 package=THT]
  LED4 = LED - 5mm [color="Red (633nm)" package="5 mm [THT]"]
  LED5 = LED - 5mm [color="Red (633nm)" package="5 mm [THT]"]
  R9 = Resistor [tolerance=±5% resistance=220 package=THT]
  R10 = Resistor [tolerance=±5% resistance=220 package=THT]
  R11 = Resistor [tolerance=±5% resistance=220 package=THT]
  R12 = Resistor [tolerance=±5% resistance=220 package=THT]
  LED6 = LED - 5mm [color="Red (633nm)" package="5 mm [THT]"]
  LED7 = LED - 5mm [color="Red (633nm)" package="5 mm [THT]"]
  R13 = Resistor [tolerance=±5% resistance=220 package=THT]
  R14 = Resistor [tolerance=±5% resistance=220 package=THT]
  R15 = Resistor [tolerance=±5% resistance=220 package=THT]
  R16 = Resistor [tolerance=±5% resistance=220 package=THT]
  LED8 = LED - 5mm [color="Red (633nm)" package="5 mm [THT]"]
  LED9 = LED - 5mm [color="Red (633nm)" package="5 mm [THT]"]
  J1 = male pin header, 4 pins [form="♂ (male)"]
  J2 = male pin header, 4 pins [form="♂ (male)"]
  OLED_I2C1 = OLED 128x64 I2C Monochrome Display
  J3 = male pin header, 7 pins [form="♂ (male)"]
  Encoder1 = Rotary encoder with push button
  3_5mm8 = 3.5mm verticle mono jack
  3_5mm3 = 3.5mm verticle mono jack
  3_5mm5 = 3.5mm verticle mono jack
  3_5mm4 = 3.5mm verticle mono jack
  3_5mm6 = 3.5mm verticle mono jack
  3_5mm7 = 3.5mm verticle mono jack
  3_5mm2 = 3.5mm verticle mono jack
  3_5mm1 = 3.5mm verticle mono jack

nets:
  N1: R1.Pin_0, 3_5mm1.Tip
  N2: R1.Pin_1, R2.Pin_0, J1.pin4
  N3: R2.Pin_1, LED2.anode
  N4: LED2.cathode, LED3.cathode, LED4.cathode, LED5.cathode, LED6.cathode, LED7.cathode, LED8.cathode, LED9.cathode, OLED_I2C1.GND, J3.pin6, Encoder1.COM, Encoder1.SPST1A, 3_5mm8.Shank, 3_5mm3.Shank, 3_5mm5.Shank, 3_5mm4.Shank, 3_5mm6.Shank, 3_5mm7.Shank, 3_5mm2.Shank, 3_5mm1.Shank
  N5: R3.Pin_0, 3_5mm2.Tip
  N6: R3.Pin_1, R4.Pin_0, J2.pin4
  N7: R4.Pin_1, LED3.anode
  N8: R5.Pin_0, 3_5mm3.Tip
  N9: R5.Pin_1, R7.Pin_0, J1.pin3
  N10: R6.Pin_0, R8.Pin_1, J2.pin3
  N11: R6.Pin_1, LED5.anode
  N12: R7.Pin_1, LED4.anode
  N13: R8.Pin_0, 3_5mm4.Tip
  N14: R9.Pin_0, 3_5mm5.Tip
  N15: R9.Pin_1, R11.Pin_0, J1.pin2
  N16: R10.Pin_0, R12.Pin_1, J2.pin2
  N17: R10.Pin_1, LED7.anode
  N18: R11.Pin_1, LED6.anode
  N19: R12.Pin_0, 3_5mm6.Tip
  N20: R13.Pin_0, 3_5mm7.Tip
  N21: R13.Pin_1, R15.Pin_0, J1.pin1
  N22: R14.Pin_0, R16.Pin_1, J2.pin1
  N23: R14.Pin_1, LED9.anode
  N24: R15.Pin_1, LED8.anode
  N25: R16.Pin_0, 3_5mm8.Tip
  N26: OLED_I2C1.SDA, J3.pin1
  N27: OLED_I2C1.SCK, J3.pin2
  N28: OLED_I2C1.VDD, J3.pin3
  N29: J3.pin4, Encoder1.SPST1B
  N30: J3.pin5, Encoder1.Encoder_B
  N31: J3.pin7, Encoder1.Encoder_A

custom parts:
  3.5mm verticle mono jack: Thonkiconn pj301m-12 verticle mono switched 3.5mm jack.
