# Fritzing sketch envelope_back (saved by Fritzing 0.9.4)
circuit board: 4cm x 10cm
perfboards: 1

parts:
  J3 = male pin header, 7 pins [form="♂ (male)"]
  NPN = NPN-Transistor [package="TO92 [THT]"]
  R1 = Resistor [tolerance=±5% resistance=10k package=THT]
  R2 = Resistor [tolerance=±5% resistance=10k package=THT]
  NPN_2 = NPN-Transistor [package="TO92 [THT]"]
  R3 = Resistor [tolerance=±5% resistance=10k package=THT]
  R4 = Resistor [tolerance=±5% resistance=10k package=THT]
  Arduino_Nano_3_0 = Arduino Nano (Rev3.0)
  IC3 = IC, DIP package, 14 pins [chip_label=MCP4922]
  IC1 = IC, DIP package, 14 pins [chip_label=MCP6004]
  J5 = shrouded pin header, 16 pins [form="♂ (shrouded male)"]
  R5 = Resistor [tolerance=±5% resistance=100k package=THT]
  R6 = Resistor [tolerance=±5% resistance=100k package=THT]
  R7 = Resistor [tolerance=±5% resistance=100k package=THT]
  R8 = Resistor [tolerance=±5% resistance=100k package=THT]
  R9 = Resistor [tolerance=±5% resistance=220 package=THT]
  R10 = Resistor [tolerance=±5% resistance=220 package=THT]
  R11 = Resistor [tolerance=±5% resistance=220 package=THT]
  R12 = Resistor [tolerance=±5% resistance=220 package=THT]
  J6 = male pin header, 9 pins [form="♂ (male)"]
  R13 = Resistor [tolerance=±5% resistance=1k package=THT]
  R14 = Resistor [tolerance=±5% resistance=1k package=THT]
  Aux = female pin header, 2 pins [form="♀ (female)"]
  C1 = Electrolytic Capacitor [capacitance=10µF package="100 mil [THT, electrolytic]"]
  C2 = Electrolytic Capacitor [capacitance=10µF package="100 mil [THT, electrolytic]"]
  R15 = Resistor [tolerance=±5% resistance=100k package=THT]
  R16 = Resistor [tolerance=±5% resistance=100k package=THT]
  R17 = Resistor [tolerance=±5% resistance=100k package=THT]
  R18 = Resistor [tolerance=±5% resistance=100k package=THT]
  R20 = Resistor [tolerance=±5% resistance=10k package=THT]
  C4 = Ceramic Capacitor [capacitance=10nF package="200 mil [THT, multilayer]"]
  C5 = Ceramic Capacitor [capacitance=10nF package="200 mil [THT, multilayer]"]
  C6 = Ceramic Capacitor [capacitance=10nF package="200 mil [THT, multilayer]"]
  C7 = Ceramic Capacitor [capacitance=10nF package="200 mil [THT, multilayer]"]
  C3 = Ceramic Capacitor [capacitance=100nF package="200 mil [THT, multilayer]"]
  470nF = Ceramic Capacitor [capacitance=0.47mF package="200 mil [THT, multilayer]"]
  LM4040-5_0 = Voltage Regulator [part_number=LM4040 package="TO92 [THT]"]

nets:
  N1: J3.pin1, R3.Pin_0, R4.Pin_1, Arduino_Nano_3_0.5V, IC3.pin1, IC3.pin9, IC3.pin11, IC3.pin13, IC1.pin4, J5.pin6, J5.pin11, C2.+, C3.1
  N2: J3.pin2, R12.Pin_1
  N3: J3.pin3, R11.Pin_1
  N4: J3.pin4, R10.Pin_1
  N5: J3.pin5, R9.Pin_1
  N6: J3.pin6, Arduino_Nano_3_0.D4
  N7: J3.pin7, NPN.E, NPN_2.E, Arduino_Nano_3_0.GND, IC3.pin8, IC3.pin12, IC1.pin3, IC1.pin5, IC1.pin10, IC1.pin11, IC1.pin12, J5.pin2, J5.pin3, J5.pin4, J5.pin13, J5.pin14, J5.pin15, J6.pin9, C1.+, C2.-, C3.0, 470nF.0
  N8: NPN.B, R1.Pin_0
  N9: NPN.C, R4.Pin_0, Arduino_Nano_3_0.D2
  N10: R1.Pin_1, J6.pin7
  N11: R2.Pin_0, NPN_2.B
  N12: R2.Pin_1, J6.pin8
  N13: NPN_2.C, R3.Pin_1, Arduino_Nano_3_0.D3
  N14: Arduino_Nano_3_0.D5, R9.Pin_0
  N15: Arduino_Nano_3_0.D6, R10.Pin_0
  N16: Arduino_Nano_3_0.D7, R11.Pin_0
  N17: Arduino_Nano_3_0.D8, R12.Pin_0
  N18: Arduino_Nano_3_0.D9, IC3.pin3
  N19: Arduino_Nano_3_0.D11/MOSI, IC3.pin5
  N20: Arduino_Nano_3_0.A5, Aux.pin1
  N21: Arduino_Nano_3_0.A4, Aux.pin2
  N22: Arduino_Nano_3_0.A3, IC1.pin8, R6.Pin_0, C5.0
  N23: Arduino_Nano_3_0.A2, IC1.pin14, R5.Pin_0, C4.0
  N24: Arduino_Nano_3_0.A1, IC1.pin7, R8.Pin_1, C7.1
  N25: Arduino_Nano_3_0.A0, IC1.pin1, R7.Pin_1, C6.1
  N26: Arduino_Nano_3_0.D13/SCK, IC3.pin4
  N27: IC3.pin10, R13.Pin_1
  N28: IC3.pin14, R14.Pin_1
  N29: IC1.pin2, R7.Pin_0, J6.pin4, R17.Pin_0, C6.0
  N30: IC1.pin6, R8.Pin_0, J6.pin5, R16.Pin_0, C7.0
  N31: IC1.pin9, R6.Pin_1, J6.pin6, R15.Pin_0, C5.1
  N32: IC1.pin13, R5.Pin_1, J6.pin3, R18.Pin_0, C4.1
  N33: J5.pin1, J5.pin16, C1.-, R20.Pin_0
  N34: J6.pin1, R13.Pin_0
  N35: J6.pin2, R14.Pin_0
  N36: R15.Pin_1, R16.Pin_1, R17.Pin_1, R18.Pin_1, LM4040-5_0.+
  N37: R20.Pin_1, 470nF.1, LM4040-5_0.-

notes:
  Envelope Back v0.4

custom parts:
  Voltage Regulator: A LM4040 shunting voltage regulator
