# Fritzing sketch envelope_front (saved by Fritzing 0.9.4)
circuit board: 4cm x 10cm
perfboards: 1

parts:
  3_5mm1 = 3.5mm verticle mono jack
  B10k = Potentiometer
  3_5mm2 = 3.5mm verticle mono jack
  B10k_2 = Potentiometer
  3_5mm3 = 3.5mm verticle mono jack
  B10k_3 = Potentiometer
  3_5mm4 = 3.5mm verticle mono jack
  B10k_4 = Potentiometer
  3_5mm5 = 3.5mm verticle mono jack
  3_5mm6 = 3.5mm verticle mono jack
  S3 = Round Pushbutton
  LED4 = LED - 3mm [color="Red (633nm)" package="3 mm [THT]"]
  LED3 = LED - 3mm [color="Red (633nm)" package="3 mm [THT]"]
  LED2 = LED - 3mm [color="Red (633nm)" package="3 mm [THT]"]
  LED1 = LED - 3mm [color="Red (633nm)" package="3 mm [THT]"]
  R5 = Resistor [tolerance=±5% resistance=100k package=THT]
  R6 = Resistor [tolerance=±5% resistance=100k package=THT]
  R7 = Resistor [tolerance=±5% resistance=100k package=THT]
  R8 = Resistor [tolerance=±5% resistance=100k package=THT]
  R10 = Resistor [tolerance=±5% resistance=200k package=THT]
  R11 = Resistor [tolerance=±5% resistance=200k package=THT]
  R12 = Resistor [tolerance=±5% resistance=200k package=THT]
  R13 = Resistor [tolerance=±5% resistance=200k package=THT]
  3_5mm7 = 3.5mm verticle mono jack
  3_5mm8 = 3.5mm verticle mono jack
  R14 = Resistor [tolerance=±5% resistance=2k package=THT]
  R15 = Resistor [tolerance=±5% resistance=2k package=THT]
  R16 = Resistor [tolerance=±5% resistance=2k package=THT]
  J1 = female pin header, 9 pins [form="♀ (female)"]
  R17 = Resistor [tolerance=±5% resistance=2k package=THT]
  J2 = female pin header, 7 pins [form="♀ (female)"]
  J3 = female pin header, 2 pins [form="♀ (female)"]
  J4 = female pin header, 1 pin [form="♀ (female)"]

nets:
  N1: 3_5mm1.Shank, B10k.CCW, B10k.Chassis#3, 3_5mm2.Shank, B10k_2.CCW, B10k_2.Chassis#3, 3_5mm3.Shank, B10k_3.CCW, B10k_3.Chassis#3, 3_5mm4.Shank, B10k_4.CCW, B10k_4.Chassis#3, 3_5mm5.Shank, 3_5mm6.Shank, S3.leg1, LED4.cathode, LED3.cathode, LED2.cathode, LED1.cathode, 3_5mm7.Shank, 3_5mm8.Shank, J1.pin1, J2.pin1, J3.pin1, J4.pin1
  N2: 3_5mm1.Tip, R6.Pin_0
  N3: B10k.WIPER, R13.Pin_0
  N4: B10k.CW, R15.Pin_0
  N5: 3_5mm2.Tip, R5.Pin_0
  N6: B10k_2.WIPER, R12.Pin_0
  N7: B10k_2.CW, R14.Pin_0
  N8: 3_5mm3.Tip, R7.Pin_0
  N9: B10k_3.WIPER, R11.Pin_0
  N10: B10k_3.CW, R16.Pin_0
  N11: 3_5mm4.Tip, R8.Pin_0
  N12: B10k_4.WIPER, R10.Pin_0
  N13: B10k_4.CW, R17.Pin_0
  N14: 3_5mm5.Tip, J1.pin2
  N15: 3_5mm6.Tip, J1.pin3
  N16: S3.leg0, J2.pin2, J3.pin2
  N17: LED4.anode, J2.pin6
  N18: LED3.anode, J2.pin5
  N19: LED2.anode, J2.pin4
  N20: LED1.anode, J2.pin3
  N21: R5.Pin_1, R12.Pin_1, J1.pin6
  N22: R6.Pin_1, R13.Pin_1, J1.pin7
  N23: R7.Pin_1, R11.Pin_1, J1.pin5
  N24: R8.Pin_1, R10.Pin_1, J1.pin4
  N25: 3_5mm7.Tip, J1.pin8
  N26: 3_5mm8.Tip, J1.pin9
  N27: R14.Pin_1, R15.Pin_1, R16.Pin_1, R17.Pin_1, J2.pin7

notes:
  switch
  LEDs
  GND
  Envelope Front v0.3

custom parts:
  3.5mm verticle mono jack: Thonkiconn pj301m-12 verticle mono switched 3.5mm jack.
  Potentiometer: Modular Addict 9mm vertical potentiometer
