# Fritzing sketch oa_front (saved by Fritzing 0.9.4)
circuit board: 2cm x 10cm
perfboards: 1

parts:
  R1 = Potentiometer
  R2 = Potentiometer
  3_5mm1 = 3.5mm verticle mono jack
  3_5mm2 = 3.5mm verticle mono jack
  R3 = Potentiometer
  R4 = Potentiometer
  3_5mm3 = 3.5mm verticle mono jack
  3_5mm4 = 3.5mm verticle mono jack
  LED1 = LED - 5mm [color="Red (633nm)" package="5 mm [THT]"]
  LED2 = LED - 5mm [color="Red (633nm)" package="5 mm [THT]"]
  J1 = female pin header, 7 pins [form="♀ (female)"]
  R5 = Resistor [tolerance=±5% resistance=470 package=THT]
  J2 = female pin header, 7 pins [form="♀ (female)"]
  R6 = Resistor [tolerance=±5% resistance=470 package=THT]
  R7 = Resistor [tolerance=±5% resistance=1k package=THT]
  R8 = Resistor [tolerance=±5% resistance=1k package=THT]
  J3 = female pin header, 1 pin [form="♀ (female)"]

nets:
  N1: R1.CCW, J1.pin7
  N2: R1.WIPER, J1.pin4
  N3: R1.CW, J1.pin6
  N4: R1.Chassis#3, R2.CW, R2.Chassis#4, 3_5mm1.Shank, 3_5mm1.Switch, 3_5mm2.Shank, R3.CW, R3.Chassis#4, R4.Chassis#3, 3_5mm3.Shank, 3_5mm3.Switch, 3_5mm4.Shank, LED1.cathode, LED2.cathode, J1.pin5, J2.pin5, J3.pin1
  N5: R2.CCW, 3_5mm1.Tip, J1.pin2
  N6: R2.WIPER, J1.pin3
  N7: 3_5mm2.Tip, R7.Pin_0
  N8: R3.CCW, 3_5mm3.Tip, J2.pin2
  N9: R3.WIPER, J2.pin3
  N10: R4.CCW, J2.pin7
  N11: R4.WIPER, J2.pin4
  N12: R4.CW, J2.pin6
  N13: 3_5mm4.Tip, R8.Pin_0
  N14: LED1.anode, R5.Pin_0
  N15: LED2.anode, R6.Pin_0
  N16: J1.pin1, R5.Pin_1, R7.Pin_1
  N17: J2.pin1, R6.Pin_1, R8.Pin_1

notes:
  GND
  O/A front
  v0.2

custom parts:
  Potentiometer: Modular Addict 9mm vertical potentiometer
  3.5mm verticle mono jack: Thonkiconn pj301m-12 verticle mono switched 3.5mm jack.
