# Fritzing sketch rng_back (saved by Fritzing 0.9.4)
circuit board: 4.9cm x 10cm
perfboards: 1

parts:
  IC1 = IC, DIP package, 28 pins [chip_label=TLC5940NT]
  Arduino_Nano_3_0 = Arduino Nano (Rev3.0)
  IC2 = IC, DIP package, 14 pins [chip_label=MCP4922]
  R2 = Resistor [tolerance=±5% resistance=10k package=THT]
  R5 = Resistor [tolerance=±5% resistance=10k package=THT]
  R7 = Resistor [tolerance=±5% resistance=10k package=THT]
  R9 = Resistor [tolerance=±5% resistance=10k package=THT]
  PNP = PNP-Transistor [package="TO92 [THT]"]
  PNP_2 = PNP-Transistor [package="TO92 [THT]"]
  PNP_3 = PNP-Transistor [package="TO92 [THT]"]
  R13 = Resistor [tolerance=±5% resistance=10k package=THT]
  R14 = Resistor [tolerance=±5% resistance=2k package=THT]
  IC3 = IC, DIP package, 8 pins [chip_label=TL072]
  C1 = Ceramic Capacitor [capacitance=100nF package="100 mil [THT, multilayer]"]
  C2 = Ceramic Capacitor [capacitance=100nF package="100 mil [THT, multilayer]"]
  J9 = shrouded pin header, 16 pins [form="♂ (shrouded male)"]
  R15 = Resistor [tolerance=±5% resistance=1k package=THT]
  J8 = male pin header, 4 pins [form="♂ (male)"]
  J2 = male pin header, 8 pins [form="♂ (male)"]
  J1 = male pin header, 7 pins [form="♂ (male)"]
  R16 = Resistor [tolerance=±5% resistance=10k package=THT]
  J7 = male pin header, 5 pins [form="♂ (male)"]
  C3 = Electrolytic Capacitor [capacitance=10µF package="100 mil [THT, electrolytic]"]
  C4 = Electrolytic Capacitor [capacitance=10µF package="100 mil [THT, electrolytic]"]
  C5 = Electrolytic Capacitor [capacitance=10µF package="100 mil [THT, electrolytic]"]

nets:
  N1: IC1.pin1, J1.pin2
  N2: IC1.pin2, J1.pin3
  N3: IC1.pin3, J1.pin4
  N4: IC1.pin4, J1.pin5
  N5: IC1.pin5, J1.pin6
  N6: IC1.pin6, J1.pin7
  N7: IC1.pin18, Arduino_Nano_3_0.D3
  N8: IC1.pin19, IC1.pin22, IC1.pin27, Arduino_Nano_3_0.GND, IC2.pin8, IC2.pin12, R7.Pin_0, PNP.C, PNP_2.C, PNP_3.C, R14.Pin_0, C1.1, J9.pin2, J9.pin3, J9.pin4, J9.pin13, J9.pin14, J9.pin15, J2.pin1, R16.Pin_0, C3.-, C4.-, C5.-
  N9: IC1.pin20, R14.Pin_1
  N10: IC1.pin21, Arduino_Nano_3_0.5V, IC2.pin1, IC2.pin9, IC2.pin11, IC2.pin13, R2.Pin_0, C1.0, J9.pin6, J9.pin11, J2.pin2, C5.+
  N11: IC1.pin23, Arduino_Nano_3_0.D10, R16.Pin_1
  N12: IC1.pin24, Arduino_Nano_3_0.D9
  N13: IC1.pin25, Arduino_Nano_3_0.D13/SCK, IC2.pin4
  N14: IC1.pin26, Arduino_Nano_3_0.D11/MOSI, IC2.pin5
  N15: IC1.pin28, J1.pin1
  N16: Arduino_Nano_3_0.D2, PNP.E
  N17: Arduino_Nano_3_0.D4, J8.pin1
  N18: Arduino_Nano_3_0.D5, J8.pin2
  N19: Arduino_Nano_3_0.D6, J7.pin5
  N20: Arduino_Nano_3_0.D7, J7.pin4
  N21: Arduino_Nano_3_0.D8, IC2.pin3
  N22: Arduino_Nano_3_0.A7, J2.pin3
  N23: Arduino_Nano_3_0.A6, J2.pin5
  N24: Arduino_Nano_3_0.A5, J2.pin4
  N25: Arduino_Nano_3_0.A4, J2.pin6
  N26: Arduino_Nano_3_0.A3, PNP_2.E
  N27: Arduino_Nano_3_0.A2, PNP_3.E
  N28: Arduino_Nano_3_0.A0, J8.pin4
  N29: IC2.pin14, IC3.pin3, J7.pin1
  N30: R2.Pin_1, R5.Pin_0, IC3.pin2
  N31: R5.Pin_1, R9.Pin_1, IC3.pin1
  N32: R7.Pin_1, R13.Pin_0, IC3.pin6
  N33: R9.Pin_0, IC3.pin5, J7.pin2
  N34: PNP.B, J8.pin3
  N35: PNP_2.B, J2.pin7
  N36: PNP_3.B, J2.pin8
  N37: R13.Pin_1, IC3.pin7, R15.Pin_1
  N38: IC3.pin4, C2.0, J9.pin1, J9.pin16, C4.+
  N39: IC3.pin8, C2.1, J9.pin5, J9.pin12, C3.+
  N40: R15.Pin_0, J7.pin3

notes:
  RNG back v0.5
  Optional
  -12v
