# Fritzing sketch rng_front (saved by Fritzing 0.9.4)
circuit board: 4.9cm x 10cm
perfboards: 1

parts:
  S1 = Toggle Switch [package=THT]
  S2 = Toggle Switch [package=THT]
  3_5mm1 = 3.5mm verticle mono jack
  3_5mm2 = 3.5mm verticle mono jack
  3_5mm3 = 3.5mm verticle mono jack
  3_5mm4 = 3.5mm verticle mono jack
  3_5mm5 = 3.5mm verticle mono jack
  3_5mm6 = 3.5mm verticle mono jack
  LED2 = LED - 5mm [color="Red (633nm)" package="5 mm [THT]"]
  LED3 = LED - 5mm [color="Red (633nm)" package="5 mm [THT]"]
  LED4 = LED - 5mm [color="Red (633nm)" package="5 mm [THT]"]
  LED5 = LED - 5mm [color="Red (633nm)" package="5 mm [THT]"]
  LED7 = LED - 5mm [color="Red (633nm)" package="5 mm [THT]"]
  R4 = Resistor [tolerance=±5% resistance=220 package=THT]
  R5 = Resistor [tolerance=±5% resistance=220 package=THT]
  R6 = Resistor [tolerance=±5% resistance=220 package=THT]
  R7 = Resistor [tolerance=±5% resistance=220 package=THT]
  R8 = Resistor [tolerance=±5% resistance=220 package=THT]
  R9 = Resistor [tolerance=±5% resistance=220 package=THT]
  R10 = Resistor [tolerance=±5% resistance=220 package=THT]
  J1 = male pin header, 7 pins [form="♂ (male)"]
  J8 = male pin header, 5 pins [form="♂ (male)"]
  J5 = male pin header, 4 pins [form="♂ (male)"]
  R11 = Resistor [tolerance=±5% resistance=1k package=THT]
  R12 = Resistor [tolerance=±5% resistance=1k package=THT]
  R13 = Resistor [tolerance=±5% resistance=1k package=THT]
  R14 = Resistor [tolerance=±5% resistance=10k package=THT]
  R15 = Resistor [tolerance=±5% resistance=10k package=THT]
  R16 = Resistor [tolerance=±5% resistance=220 package=THT]
  R17 = Resistor [tolerance=±5% resistance=220 package=THT]
  J4 = male pin header, 8 pins [form="♂ (male)"]
  LED1 = LED - 5mm [color="Red (633nm)" package="5 mm [THT]"]
  LED6 = LED - 5mm [color="Red (633nm)" package="5 mm [THT]"]
  LED8 = LED - 3mm [color="Red (633nm)" package="3 mm [THT]"]
  LED9 = LED - 3mm [color="Red (633nm)" package="3 mm [THT]"]
  Encoder1 = Rotary encoder with push button
  R2 = Potentiometer
  R1 = Potentiometer
  R3 = Potentiometer

nets:
  N1: S1.L1, J8.pin5
  N2: S1.COM, J8.pin4
  GND: S2.L1, 3_5mm1.Shank, 3_5mm1.Switch, 3_5mm2.Shank, 3_5mm3.Shank, 3_5mm4.Shank, 3_5mm5.Shank, 3_5mm5.Switch, 3_5mm6.Shank, 3_5mm6.Switch, J4.pin1, LED8.cathode, LED9.cathode, Encoder1.COM, Encoder1.SPST1B, R2.CCW, R2.Chassis#3, R1.CCW, R1.Chassis#3, R3.CCW, R3.Chassis#3
  N3: S2.COM, J5.pin4
  N4: S2.L2, R4.Pin_0, R5.Pin_0, R6.Pin_0, R7.Pin_0, R8.Pin_0, R9.Pin_0, R10.Pin_0, J4.pin2, R2.CW, R1.CW, R3.CW
  N5: 3_5mm1.Tip, R11.Pin_1
  N6: 3_5mm2.Tip, J8.pin3
  N7: 3_5mm3.Tip, R15.Pin_1
  N8: 3_5mm4.Tip, R14.Pin_1
  N9: 3_5mm5.Tip, R12.Pin_1
  N10: 3_5mm6.Tip, R13.Pin_1
  N11: LED2.cathode, J1.pin2
  N12: LED2.anode, R9.Pin_1
  N13: LED3.cathode, J1.pin3
  N14: LED3.anode, R8.Pin_1
  N15: LED4.cathode, J1.pin4
  N16: LED4.anode, R7.Pin_1
  N17: LED5.cathode, J1.pin5
  N18: LED5.anode, R6.Pin_1
  N19: LED7.cathode, J1.pin7
  N20: LED7.anode, R4.Pin_1
  N21: R5.Pin_1, LED6.anode
  N22: R10.Pin_1, LED1.anode
  N23: J1.pin1, LED1.cathode
  N24: J1.pin6, LED6.cathode
  N25: J8.pin1, R14.Pin_0, R16.Pin_1
  N26: J8.pin2, R15.Pin_0, R17.Pin_1
  N27: J5.pin1, Encoder1.Encoder_B
  N28: J5.pin2, Encoder1.Encoder_A
  N29: J5.pin3, R11.Pin_0
  N30: R12.Pin_0, J4.pin8
  N31: R13.Pin_0, J4.pin7
  N32: R16.Pin_0, LED8.anode
  N33: R17.Pin_0, LED9.anode
  N34: J4.pin3, R1.WIPER
  N35: J4.pin4, Encoder1.SPST1A
  N36: J4.pin5, R3.WIPER
  N37: J4.pin6, R2.WIPER

custom parts:
  3.5mm verticle mono jack: Thonkiconn pj301m-12 verticle mono switched 3.5mm jack.
  Potentiometer: Modular Addict 9mm vertical potentiometer
