# Fritzing sketch rng_back (saved by Fritzing 0.9.4)
circuit board: 4.9cm x 10cm
perfboards: 1

parts:
  J1 = male pin header, 7 pins [form="♂ (male)"]
  IC1 = IC, DIP package, 28 pins [chip_label=TLC5940NT]
  Part1 = Arduino Nano (Rev3.0)
  R1 = Resistor [tolerance=±5% resistance=220 package=THT]
  IC2 = IC, DIP package, 14 pins [chip_label=MCP4922]
  IC3 = IC, DIP package, 8 pins [chip_label=TL072]
  R2 = Resistor [tolerance=±5% resistance=10k package=THT]
  J3 = male pin header, 3 pins [form="♂ (male)"]
  J4 = male pin header, 3 pins [form="♂ (male)"]
  J5 = male pin header, 3 pins [form="♂ (male)"]
  J6 = male pin header, 3 pins [form="♂ (male)"]
  R5 = Resistor [tolerance=±5% resistance=10k package=THT]
  R7 = Resistor [tolerance=±5% resistance=10k package=THT]
  R9 = Resistor [tolerance=±5% resistance=10k package=THT]
  J7 = male pin header, 5 pins [form="♂ (male)"]
  J2 = male pin header, 8 pins [form="♂ (male)"]
  J8 = male pin header, 4 pins [form="♂ (male)"]
  Q1 = PNP-Transistor [package="TO92 [THT]"]
  R10 = Resistor [tolerance=±5% resistance=10k package=THT]
  Q2 = PNP-Transistor [package="TO92 [THT]"]
  R11 = Resistor [tolerance=±5% resistance=10k package=THT]
  Q3 = PNP-Transistor [package="TO92 [THT]"]
  R12 = Resistor [tolerance=±5% resistance=10k package=THT]
  R13 = Resistor [tolerance=±5% resistance=10k package=THT]

nets:
  N1: J1.pin1, IC1.pin28
  N2: J1.pin2, IC1.pin1
  N3: J1.pin3, IC1.pin2
  N4: J1.pin4, IC1.pin3
  N5: J1.pin5, IC1.pin4
  N6: J1.pin6, IC1.pin5
  N7: J1.pin7, IC1.pin6
  N8: IC1.pin18, Part1.D3
  N9: IC1.pin20, R1.Pin_1
  N10: IC1.pin21, Part1.5V, IC2.pin1, IC2.pin9, IC2.pin11, IC2.pin13, R2.Pin_0, J6.pin1, J6.pin2, J6.pin3, J2.pin2, R10.Pin_1, R11.Pin_1, R12.Pin_1
  N11: IC1.pin22, IC1.pin27, Part1.GND, R1.Pin_0, IC2.pin8, IC2.pin12, J4.pin1, J4.pin2, J4.pin3, R7.Pin_0, J2.pin1, Q1.C, Q2.C, Q3.C
  N12: IC1.pin23, Part1.D10
  N13: IC1.pin24, Part1.D9
  N14: IC1.pin25, Part1.D13/SCK
  N15: IC1.pin26, Part1.D11/MOSI, IC2.pin5
  N16: Part1.D2, Q1.E, R10.Pin_0
  N17: Part1.D4, J8.pin1
  N18: Part1.D5, J8.pin2
  N19: Part1.D6, J7.pin5
  N20: Part1.D7, J7.pin4
  N21: Part1.D8, IC2.pin3
  N22: Part1.A7, J2.pin3
  N23: Part1.A6, J2.pin4
  N24: Part1.A5, J2.pin5
  N25: Part1.A4, J2.pin6
  N26: Part1.A3, Q2.E, R11.Pin_0
  N27: Part1.A0, J8.pin4
  N28: Part1.3V3, IC2.pin4
  N29: IC3.pin1, R5.Pin_1, R9.Pin_1
  N30: IC3.pin2, R2.Pin_1, R5.Pin_0
  N31: IC3.pin3, J7.pin3
  N32: IC3.pin4, J3.pin1, J3.pin2, J3.pin3
  N33: IC3.pin5, R9.Pin_0, J7.pin2
  N34: IC3.pin6, R7.Pin_1, R13.Pin_0
  N35: IC3.pin7, J7.pin1, R13.Pin_1
  N36: IC3.pin8, J5.pin1, J5.pin2, J5.pin3
  N37: J2.pin7, Q2.B
  N38: J2.pin8, Q3.B
  N39: J8.pin3, Q1.B
  N40: Q3.E, R12.Pin_0
