# Fritzing sketch rng_front (saved by Fritzing 0.9.4)
circuit board: 4.9cm x 10cm
perfboards: 1

parts:
  R1 = Potentiometer
  R2 = Potentiometer
  R3 = Potentiometer
  Encoder1 = Rotary encoder with push button
  S1 = Toggle Switch [package=THT]
  S2 = Toggle Switch [package=THT]
  3_5mm1 = 3.5mm verticle mono jack
  3_5mm2 = 3.5mm verticle mono jack
  3_5mm3 = 3.5mm verticle mono jack
  3_5mm4 = 3.5mm verticle mono jack
  3_5mm5 = 3.5mm verticle mono jack
  3_5mm6 = 3.5mm verticle mono jack
  LED1 = LED - 5mm [color="Red (633nm)" package="5 mm [THT]"]
  LED2 = LED - 5mm [color="Red (633nm)" package="5 mm [THT]"]
  LED3 = LED - 5mm [color="Red (633nm)" package="5 mm [THT]"]
  LED4 = LED - 5mm [color="Red (633nm)" package="5 mm [THT]"]
  LED5 = LED - 5mm [color="Red (633nm)" package="5 mm [THT]"]
  LED6 = LED - 5mm [color="Red (633nm)" package="5 mm [THT]"]
  LED7 = LED - 5mm [color="Red (633nm)" package="5 mm [THT]"]
  R4 = Resistor [tolerance=±5% resistance=220 package=THT]
  R5 = Resistor [tolerance=±5% resistance=220 package=THT]
  R6 = Resistor [tolerance=±5% resistance=220 package=THT]
  R7 = Resistor [tolerance=±5% resistance=220 package=THT]
  R8 = Resistor [tolerance=±5% resistance=220 package=THT]
  R9 = Resistor [tolerance=±5% resistance=220 package=THT]
  R10 = Resistor [tolerance=±5% resistance=220 package=THT]
  J1 = male pin header, 7 pins [form="♂ (male)"]
  J8 = male pin header, 5 pins [form="♂ (male)"]
  J5 = male pin header, 4 pins [form="♂ (male)"]
  R11 = Resistor [tolerance=±5% resistance=10k package=THT]
  R12 = Resistor [tolerance=±5% resistance=10k package=THT]
  R13 = Resistor [tolerance=±5% resistance=10k package=THT]
  R14 = Resistor [tolerance=±5% resistance=10k package=THT]
  R15 = Resistor [tolerance=±5% resistance=10k package=THT]
  LED8 = LED - 5mm [color="Red (633nm)" package="5 mm [THT]"]
  LED9 = LED - 5mm [color="Red (633nm)" package="5 mm [THT]"]
  R16 = Resistor [tolerance=±5% resistance=220 package=THT]
  R17 = Resistor [tolerance=±5% resistance=220 package=THT]
  J4 = male pin header, 8 pins [form="♂ (male)"]

nets:
  N1: R1.CCW, R2.CCW, J4.pin1
  N2: R1.WIPER, J4.pin3
  N3: R1.CW, R2.CW, R3.CW, S2.L2, R4.Pin_0, R5.Pin_0, R6.Pin_0, R7.Pin_0, R8.Pin_0, R9.Pin_0, R10.Pin_0, J4.pin2
  N4: R2.WIPER, J4.pin6
  N5: R3.CCW, Encoder1.COM, Encoder1.SPST1B, S2.L1, 3_5mm1.Shank, 3_5mm2.Shank, 3_5mm3.Shank, 3_5mm4.Shank, 3_5mm5.Shank, 3_5mm6.Shank, LED8.cathode, LED9.cathode
  N6: R3.WIPER, J4.pin5
  N7: Encoder1.Encoder_A, J5.pin2
  N8: Encoder1.Encoder_B, J5.pin1
  N9: Encoder1.SPST1A, J4.pin4
  N10: S1.L1, J8.pin5
  N11: S1.COM, J8.pin4
  N12: S2.COM, J5.pin4
  N13: 3_5mm1.Tip, R11.Pin_1
  N14: 3_5mm2.Tip, J8.pin3
  N15: 3_5mm3.Tip, R15.Pin_1
  N16: 3_5mm4.Tip, R14.Pin_1
  N17: 3_5mm5.Tip, R12.Pin_1
  N18: 3_5mm6.Tip, R13.Pin_1
  N19: LED1.cathode, J1.pin1
  N20: LED1.anode, R10.Pin_1
  N21: LED2.cathode, J1.pin2
  N22: LED2.anode, R9.Pin_1
  N23: LED3.cathode, J1.pin3
  N24: LED3.anode, R8.Pin_1
  N25: LED4.cathode, J1.pin4
  N26: LED4.anode, R7.Pin_1
  N27: LED5.cathode, J1.pin5
  N28: LED5.anode, R6.Pin_1
  N29: LED6.cathode, J1.pin6
  N30: LED6.anode, R5.Pin_1
  N31: LED7.cathode, J1.pin7
  N32: LED7.anode, R4.Pin_1
  N33: J8.pin1, R14.Pin_0, R16.Pin_1
  N34: J8.pin2, R15.Pin_0, R17.Pin_1
  N35: J5.pin3, R11.Pin_0
  N36: R12.Pin_0, J4.pin8
  N37: R13.Pin_0, J4.pin7
  N38: LED8.anode, R16.Pin_0
  N39: LED9.anode, R17.Pin_0

custom parts:
  Potentiometer: Modular Addict 9mm vertical potentiometer
  3.5mm verticle mono jack: Thonkiconn pj301m-12 verticle mono switched 3.5mm jack.
