# Fritzing sketch sequencer_pcb_back (saved by Fritzing 0.9.4)
circuit board: 12.15cm x 10cm
perfboards: 1

parts:
  IC1 = IC, DIP package, 16 pins [chip_label=CD4051be]
  IC2 = IC, DIP package, 16 pins [chip_label=CD4051be]
  J17 = female pin header, 5 pins [form="♀ (female)"]
  IC3 = IC, DIP package, 28 pins [chip_label=MCP23S17]
  J18 = female pin header, 2 pins [form="♀ (female)"]
  Part1 = Arduino Nano (Rev3.0) [part_number="Arduino Nano 3.0"]
  IC4 = IC, DIP package, 14 pins [chip_label=MCP4922]
  IC5 = IC, DIP package, 14 pins [chip_label=MCP4922]
  IC6 = IC, DIP package, 28 pins [chip_label=MCP23S17]
  R1 = Resistor [tolerance=±5% resistance=1k package=THT]
  R2 = Resistor [tolerance=±5% resistance=1k package=THT]
  R3 = Resistor [tolerance=±5% resistance=1k package=THT]
  R4 = Resistor [tolerance=±5% resistance=1k package=THT]
  R5 = Resistor [tolerance=±5% resistance=100k package=THT]
  R6 = Resistor [tolerance=±5% resistance=100k package=THT]
  R7 = Resistor [tolerance=±5% resistance=100k package=THT]
  R8 = Resistor [tolerance=±5% resistance=100k package=THT]
  R9 = Resistor [tolerance=±5% resistance=100k package=THT]
  R10 = Resistor [tolerance=±5% resistance=100k package=THT]
  R11 = Resistor [tolerance=±5% resistance=100k package=THT]
  R12 = Resistor [tolerance=±5% resistance=100k package=THT]
  NPN = NPN-Transistor [package="TO92 [THT]"]
  NPN_2 = NPN-Transistor [package="TO92 [THT]"]
  NPN_3 = NPN-Transistor [package="TO92 [THT]"]
  R13 = Resistor [tolerance=±5% resistance=100k package=THT]
  R14 = Resistor [tolerance=±5% resistance=100k package=THT]
  NPN_4 = NPN-Transistor [package="TO92 [THT]"]
  NPN_5 = NPN-Transistor [package="TO92 [THT]"]
  R15 = Resistor [tolerance=±5% resistance=100k package=THT]
  R16 = Resistor [tolerance=±5% resistance=100k package=THT]
  R17 = Resistor [tolerance=±5% resistance=100k package=THT]
  R18 = Resistor [tolerance=±5% resistance=100k package=THT]
  R19 = Resistor [tolerance=±5% resistance=100k package=THT]
  R20 = Resistor [tolerance=±5% resistance=100k package=THT]
  R21 = Resistor [tolerance=±5% resistance=100k package=THT]
  R22 = Resistor [tolerance=±5% resistance=100k package=THT]
  NPN_6 = NPN-Transistor [package="TO92 [THT]"]
  NPN_7 = NPN-Transistor [package="TO92 [THT]"]
  NPN_8 = NPN-Transistor [package="TO92 [THT]"]
  NPN_9 = NPN-Transistor [package="TO92 [THT]"]
  J19 = shrouded pin header, 16 pins [form="♂ (shrouded male)"]
  J22 = female pin header, 1 pin [form="♀ (female)"]
  J15 = male pin header, 4 pins [form="♂ (male)"]
  J20 = male pin header, 7 pins [form="♂ (male)"]
  J11 = male pin header, 4 pins [form="♂ (male)"]
  J7 = male pin header, 4 pins [form="♂ (male)"]
  J8 = male pin header, 10 pins [form="♂ (male)"]
  J10 = male pin header, 4 pins [form="♂ (male)"]
  J21 = male pin header, 6 pins [form="♂ (male)"]
  J9 = male pin header, 4 pins [form="♂ (male)"]
  C1 = Electrolytic Capacitor [capacitance=10µF package="100 mil [THT, electrolytic]"]
  C2 = Ceramic Capacitor [capacitance=100nF package="100 mil [THT, multilayer]"]
  C3 = Ceramic Capacitor [capacitance=100nF package="100 mil [THT, multilayer]"]
  J23 = female pin header, 1 pin [form="♀ (female)"]
  J24 = female pin header, 8 pins [form="♀ (female)"]
  J26 = female pin header, 2 pins [form="♀ (female)"]
  J25 = female pin header, 2 pins [form="♀ (female)"]

nets:
  N1: IC1.pin1, J21.pin2
  N2: IC1.pin2, J21.pin3
  N3: IC1.pin3, Part1.A7
  N4: IC1.pin4, J21.pin4
  N5: IC1.pin5, J21.pin5
  N6: IC1.pin8, IC2.pin8, IC3.pin10, IC3.pin15, IC3.pin16, IC3.pin17, Part1.GND, IC6.pin10, IC6.pin16, IC6.pin17, R19.Pin_0, R20.Pin_0, R21.Pin_0, R22.Pin_0, NPN_6.E, NPN_7.E, NPN_8.E, NPN_9.E, J22.pin1, J8.pin1
  N7: IC1.pin9, IC2.pin9, Part1.D6
  N8: IC1.pin10, IC2.pin10, Part1.D5
  N9: IC1.pin11, IC2.pin11, Part1.D4
  N10: IC1.pin12, J11.pin4
  N11: IC1.pin13, J11.pin3
  N12: IC1.pin14, J11.pin2
  N13: IC1.pin15, J11.pin1
  N14: IC1.pin16, IC2.pin16, IC3.pin9, IC3.pin18, Part1.5V, IC4.pin1, IC4.pin9, IC4.pin11, IC4.pin13, IC5.pin1, IC5.pin9, IC5.pin11, IC5.pin13, IC6.pin9, IC6.pin15, IC6.pin18, J19.pin6, J19.pin11, J8.pin10, C1.+, C2.0, C3.0
  N15: IC2.pin1, J20.pin3
  N16: IC2.pin2, J20.pin4
  N17: IC2.pin3, Part1.A6
  N18: IC2.pin4, J20.pin5
  N19: IC2.pin5, J20.pin6
  N20: IC2.pin12, J15.pin4
  N21: IC2.pin13, J15.pin3
  N22: IC2.pin14, J15.pin2
  N23: IC2.pin15, J15.pin1
  N24: J17.pin1, IC3.pin6
  N25: J17.pin2, IC3.pin5
  N26: J17.pin3, IC3.pin4
  N27: J17.pin4, IC3.pin3
  N28: J17.pin5, IC3.pin2
  N29: IC3.pin1, NPN_2.C
  N30: IC3.pin7, J18.pin1
  N31: IC3.pin8, J18.pin2
  N32: IC3.pin11, Part1.D7
  N33: IC3.pin12, Part1.D13/SCK, IC4.pin4, IC5.pin4, IC6.pin12
  N34: IC3.pin13, Part1.D11/MOSI, IC4.pin5, IC5.pin5, IC6.pin13
  N35: IC3.pin14, Part1.D12/MISO, IC6.pin14
  N36: IC3.pin19, Part1.D2
  N37: IC3.pin20, Part1.D3
  N38: IC3.pin21, NPN_3.C
  N39: IC3.pin22, NPN.C
  N40: IC3.pin23, NPN_4.C
  N41: IC3.pin24, NPN_5.C
  N42: IC3.pin25, NPN_6.C
  N43: IC3.pin26, NPN_7.C
  N44: IC3.pin27, NPN_8.C
  N45: IC3.pin28, NPN_9.C
  N46: Part1.D8, IC6.pin11
  N47: Part1.D9, IC4.pin3
  N48: Part1.D10, IC5.pin3
  N49: Part1.A5, R4.Pin_1
  N50: Part1.A4, R3.Pin_1
  N51: Part1.A3, R2.Pin_1
  N52: Part1.A2, R1.Pin_1
  N53: Part1.A1, J26.pin1
  N54: Part1.A0, J26.pin2
  N55: IC4.pin8, IC4.pin12, IC5.pin8, IC5.pin12, J19.pin2, J19.pin3, J19.pin4, J19.pin13, J19.pin14, J19.pin15, C1.-, C2.1, C3.1, J23.pin1
  N56: IC4.pin10, J9.pin2
  N57: IC4.pin14, J9.pin1
  N58: IC5.pin10, J9.pin4
  N59: IC5.pin14, J9.pin3
  N60: IC6.pin1, J8.pin9
  N61: IC6.pin2, J8.pin7
  N62: IC6.pin3, J8.pin5
  N63: IC6.pin4, J8.pin3
  N64: IC6.pin5, J8.pin8
  N65: IC6.pin6, J8.pin6
  N66: IC6.pin7, J8.pin4
  N67: IC6.pin8, J8.pin2
  N68: IC6.pin19, J25.pin1
  N69: IC6.pin20, J25.pin2
  N70: IC6.pin21, J24.pin1
  N71: IC6.pin22, J24.pin2
  N72: IC6.pin23, J24.pin3
  N73: IC6.pin24, J24.pin4
  N74: IC6.pin25, J24.pin5
  N75: IC6.pin26, J24.pin6
  N76: IC6.pin27, J24.pin7
  N77: IC6.pin28, J24.pin8
  N78: R1.Pin_0, J10.pin4
  N79: R2.Pin_0, J10.pin3
  N80: R3.Pin_0, J10.pin2
  N81: R4.Pin_0, J10.pin1
  N82: R5.Pin_0, J20.pin2
  N83: R5.Pin_1, R10.Pin_1, NPN_3.B
  N84: R6.Pin_0, J20.pin7
  N85: R6.Pin_1, R9.Pin_1, NPN.B
  N86: R7.Pin_0, J21.pin1
  N87: R7.Pin_1, R13.Pin_0, NPN_4.B
  N88: R8.Pin_0, J21.pin6
  N89: R8.Pin_1, R14.Pin_0, NPN_5.B
  N90: R9.Pin_0, NPN.E
  N91: R10.Pin_0, NPN_3.E
  N92: R11.Pin_0, J20.pin1
  N93: R11.Pin_1, R12.Pin_1, NPN_2.B
  N94: R12.Pin_0, NPN_2.E
  N95: R13.Pin_1, NPN_4.E
  N96: R14.Pin_1, NPN_5.E
  N97: R15.Pin_0, J7.pin4
  N98: R15.Pin_1, R19.Pin_1, NPN_9.B
  N99: R16.Pin_0, J7.pin3
  N100: R16.Pin_1, R20.Pin_1, NPN_8.B
  N101: R17.Pin_0, J7.pin2
  N102: R17.Pin_1, R21.Pin_1, NPN_7.B
  N103: R18.Pin_0, J7.pin1
  N104: R18.Pin_1, R22.Pin_1, NPN_6.B

notes:
  -12v
  rotary
  switch
  GND
  Sequencer back v0.1
  Switch
