# Fritzing sketch sequencer_pcb_front (saved by Fritzing 0.9.4)
circuit board: 12.15cm x 10cm
perfboards: 1

parts:
  R1 = Potentiometer
  R2 = Potentiometer
  R3 = Potentiometer
  R4 = Potentiometer
  R5 = Potentiometer
  R6 = Potentiometer
  R7 = Potentiometer
  R8 = Potentiometer
  R9 = Potentiometer
  R10 = Potentiometer
  R11 = Potentiometer
  R12 = Potentiometer
  R13 = Potentiometer
  R14 = Potentiometer
  R15 = Potentiometer
  R16 = Potentiometer
  3_5mm1 = 3.5mm verticle mono jack
  3_5mm2 = 3.5mm verticle mono jack
  3_5mm3 = 3.5mm verticle mono jack
  3_5mm4 = 3.5mm verticle mono jack
  3_5mm5 = 3.5mm verticle mono jack
  3_5mm6 = 3.5mm verticle mono jack
  3_5mm7 = 3.5mm verticle mono jack
  3_5mm8 = 3.5mm verticle mono jack
  3_5mm9 = 3.5mm verticle mono jack
  3_5mm10 = 3.5mm verticle mono jack
  3_5mm11 = 3.5mm verticle mono jack
  3_5mm12 = 3.5mm verticle mono jack
  3_5mm13 = 3.5mm verticle mono jack
  3_5mm14 = 3.5mm verticle mono jack
  3_5mm15 = 3.5mm verticle mono jack
  3_5mm16 = 3.5mm verticle mono jack
  3_5mm17 = 3.5mm verticle mono jack
  LED1 = LED - 3mm [color="Red (633nm)" package="3 mm [THT]"]
  LED2 = LED - 3mm [color="Red (633nm)" package="3 mm [THT]"]
  LED3 = LED - 3mm [color="Red (633nm)" package="3 mm [THT]"]
  LED4 = LED - 3mm [color="Red (633nm)" package="3 mm [THT]"]
  LED5 = LED - 3mm [color="Red (633nm)" package="3 mm [THT]"]
  LED6 = LED - 3mm [color="Red (633nm)" package="3 mm [THT]"]
  LED7 = LED - 3mm [color="Red (633nm)" package="3 mm [THT]"]
  LED8 = LED - 3mm [color="Red (633nm)" package="3 mm [THT]"]
  LED9 = LED - 3mm [color="Red (633nm)" package="3 mm [THT]"]
  LED10 = LED - 3mm [color="Red (633nm)" package="3 mm [THT]"]
  LED11 = LED - 3mm [color="Red (633nm)" package="3 mm [THT]"]
  LED12 = LED - 3mm [color="Red (633nm)" package="3 mm [THT]"]
  LED13 = LED - 3mm [color="Red (633nm)" package="3 mm [THT]"]
  LED14 = LED - 3mm [color="Red (633nm)" package="3 mm [THT]"]
  LED15 = LED - 3mm [color="Red (633nm)" package="3 mm [THT]"]
  LED16 = LED - 3mm [color="Red (633nm)" package="3 mm [THT]"]
  S2 = male pin header, 2 pins [form="♂ (male)"]
  S1 = male pin header, 2 pins [form="♂ (male)"]
  S4 = male pin header, 2 pins [form="♂ (male)"]
  S3 = male pin header, 2 pins [form="♂ (male)"]
  LED17 = LED - 3mm [color="Red (633nm)" package="3 mm [THT]"]
  R19 = Resistor [tolerance=±5% resistance=220 package=THT]
  R20 = Resistor [tolerance=±5% resistance=1k package=THT]
  LED18 = LED - 3mm [color="Red (633nm)" package="3 mm [THT]"]
  R21 = Resistor [tolerance=±5% resistance=1k package=THT]
  R22 = Resistor [tolerance=±5% resistance=220 package=THT]
  LED19 = LED - 3mm [color="Red (633nm)" package="3 mm [THT]"]
  R23 = Resistor [tolerance=±5% resistance=1k package=THT]
  R24 = Resistor [tolerance=±5% resistance=220 package=THT]
  LED20 = LED - 3mm [color="Red (633nm)" package="3 mm [THT]"]
  R25 = Resistor [tolerance=±5% resistance=1k package=THT]
  R26 = Resistor [tolerance=±5% resistance=220 package=THT]
  (S5) = female pin header, 2 pins [form="♀ (female)"]
  J17 = female pin header, 6 pins [form="♀ (female)"]
  J3 = female pin header, 4 pins [form="♀ (female)"]
  J16 = female pin header, 7 pins [form="♀ (female)"]
  J13 = female pin header, 4 pins [form="♀ (female)"]
  J14 = female pin header, 4 pins [form="♀ (female)"]
  J6 = female pin header, 4 pins [form="♀ (female)"]
  J1 = female pin header, 4 pins [form="♀ (female)"]
  J15 = female pin header, 10 pins [form="♀ (female)"]
  R27 = Resistor [tolerance=±5% resistance=1k package=THT]

nets:
  N1: R1.CCW, R1.Chassis#3, R2.CCW, R2.Chassis#4, R3.CCW, R3.Chassis, R4.CCW, R4.Chassis#4, R5.CCW, R5.Chassis, R6.CCW, R6.Chassis, R7.CCW, R7.Chassis, R8.CCW, R8.Chassis#3, R9.CCW, R9.Chassis, R10.CCW, R10.Chassis, R11.CCW, R11.Chassis, R12.CCW, R12.Chassis#3, R13.CCW, R13.Chassis#3, R14.CCW, R14.Chassis#3, R15.CCW, R15.Chassis#3, R16.CCW, R16.Chassis#3, 3_5mm1.Shank, 3_5mm1.Switch, 3_5mm2.Shank, 3_5mm3.Shank, 3_5mm4.Shank, 3_5mm5.Shank, 3_5mm6.Shank, 3_5mm7.Shank, 3_5mm8.Shank, 3_5mm9.Shank, 3_5mm10.Shank, 3_5mm11.Shank, 3_5mm12.Shank, 3_5mm13.Shank, 3_5mm14.Shank, 3_5mm15.Shank, 3_5mm16.Shank, 3_5mm17.Shank, LED17.cathode, LED18.cathode, LED19.cathode, LED20.cathode, J15.pin10
  N2: R1.WIPER, J1.pin4
  N3: R1.CW, R2.CW, R3.CW, R4.CW, R5.CW, R6.CW, R7.CW, R8.CW, R9.CW, R10.CW, R11.CW, R12.CW, R13.CW, R14.CW, R15.CW, R16.CW, S2.pin1, S1.pin1, S4.pin1, S3.pin1, (S5).pin2, J15.pin1, R27.Pin_0, R27.Pin_1
  N4: R2.WIPER, J1.pin3
  N5: R3.WIPER, J1.pin1
  N6: R4.WIPER, J1.pin2
  N7: R5.WIPER, J17.pin4
  N8: R6.WIPER, J17.pin5
  N9: R7.WIPER, J17.pin3
  N10: R8.WIPER, J17.pin2
  N11: R9.WIPER, J3.pin2
  N12: R10.WIPER, J3.pin1
  N13: R11.WIPER, J3.pin3
  N14: R12.WIPER, J3.pin4
  N15: R13.WIPER, J16.pin4
  N16: R14.WIPER, J16.pin5
  N17: R15.WIPER, J16.pin3
  N18: R16.WIPER, J16.pin2
  N19: 3_5mm1.Tip, 3_5mm2.Switch, 3_5mm3.Switch, J6.pin4
  N20: 3_5mm2.Tip, J6.pin3
  N21: 3_5mm3.Tip, 3_5mm4.Switch, J6.pin2
  N22: 3_5mm4.Tip, J6.pin1
  N23: 3_5mm5.Tip, R23.Pin_1
  N24: 3_5mm6.Tip, R20.Pin_1
  N25: 3_5mm7.Tip, R25.Pin_1
  N26: 3_5mm8.Tip, R21.Pin_1
  N27: 3_5mm9.Tip, S1.pin2, J17.pin1
  N28: 3_5mm10.Tip, S2.pin2, J17.pin6
  N29: 3_5mm11.Tip, S4.pin2, J16.pin6
  N30: 3_5mm12.Tip, S3.pin2, J16.pin1
  N31: 3_5mm13.Tip, J13.pin2
  N32: 3_5mm14.Tip, J13.pin4
  N33: 3_5mm15.Tip, J13.pin1
  N34: 3_5mm16.Tip, J13.pin3
  N35: 3_5mm17.Tip, (S5).pin1, J16.pin7
  N36: LED1.cathode, LED2.cathode, LED3.cathode, LED4.cathode, J15.pin2
  N37: LED1.anode, LED8.anode, LED12.anode, LED16.anode, J15.pin3
  N38: LED2.anode, LED7.anode, LED11.anode, LED15.anode, J15.pin5
  N39: LED3.anode, LED5.anode, LED9.anode, LED13.anode, J15.pin7
  N40: LED4.anode, LED6.anode, LED10.anode, LED14.anode, J15.pin9
  N41: LED5.cathode, LED6.cathode, LED7.cathode, LED8.cathode, J15.pin4
  N42: LED9.cathode, LED10.cathode, LED11.cathode, LED12.cathode, J15.pin6
  N43: LED13.cathode, LED14.cathode, LED15.cathode, LED16.cathode, J15.pin8
  N44: LED17.anode, R19.Pin_1
  N45: R19.Pin_0, R20.Pin_0, J14.pin2
  N46: LED18.anode, R22.Pin_1
  N47: R21.Pin_0, R22.Pin_0, J14.pin1
  N48: LED19.anode, R24.Pin_1
  N49: R23.Pin_0, R24.Pin_0, J14.pin3
  N50: LED20.anode, R26.Pin_1
  N51: R25.Pin_0, R26.Pin_0, J14.pin4

notes:
  ----------
  ------
  ----
  Sequencer Front v0.1

custom parts:
  Potentiometer: Modular Addict 9mm vertical potentiometer
  3.5mm verticle mono jack: Thonkiconn pj301m-12 verticle mono switched 3.5mm jack.
