# Fritzing sketch Simplex PCB middle (saved by Fritzing 0.9.4)
circuit board: 2cm x 10cm
perfboards: 1

parts:
  IC1 = IC, DIP package, 14 pins [chip_label=MCP4922]
  PNP = PNP-Transistor [package="TO92 [THT]"]
  PNP_2 = PNP-Transistor [package="TO92 [THT]"]
  IC2 = IC, DIP package, 8 pins [chip_label=TL072]
  J3 = male pin header, 5 pins [form="♂ (male)"]
  R1 = Resistor [tolerance=±5% resistance=1k package=THT]
  R2 = Resistor [tolerance=±5% resistance=1k package=THT]
  R3 = Resistor [tolerance=±5% resistance=220 package=THT]
  R4 = Resistor [tolerance=±5% resistance=220 package=THT]
  R5 = Resistor [tolerance=±5% resistance=1k package=THT]
  R6 = Resistor [tolerance=±5% resistance=1k package=THT]
  R7 = Resistor [tolerance=±5% resistance=1k package=THT]
  R8 = Resistor [tolerance=±5% resistance=1k package=THT]
  R9 = Resistor [tolerance=±5% resistance=1k package=THT]
  R10 = Resistor [tolerance=±5% resistance=1M package=THT]
  R11 = Resistor [tolerance=±5% resistance=1M package=THT]
  R12 = Resistor [tolerance=±5% resistance=1k package=THT]
  R13 = Resistor [tolerance=±5% resistance=1k package=THT]
  J4 = male pin header, 5 pins [form="♂ (male)"]
  J5 = male pin header, 3 pins [form="♂ (male)"]
  J6 = male pin header, 5 pins [form="♂ (male)"]
  J7 = male pin header, 4 pins [form="♂ (male)"]
  J8 = male pin header, 2 pins [form="♂ (male)"]
  C1 = Ceramic Capacitor [capacitance=100nF package="100 mil [THT, multilayer]"]
  C2 = Ceramic Capacitor [capacitance=100nF package="100 mil [THT, multilayer]"]

nets:
  N1: IC1.pin1, IC1.pin9, IC1.pin11, IC1.pin13, R9.Pin_1, R10.Pin_1, R11.Pin_1, J7.pin2, J8.pin2, C1.1
  N2: IC1.pin3, J5.pin3
  N3: IC1.pin4, J5.pin1
  N4: IC1.pin5, J5.pin2
  N5: IC1.pin8, IC1.pin12, PNP.C, PNP_2.C, J3.pin3, R6.Pin_1, J7.pin1, J8.pin1, C1.0
  N6: IC1.pin10, R1.Pin_0, R3.Pin_0
  N7: IC1.pin14, IC2.pin3, R4.Pin_0
  N8: PNP.E, R11.Pin_0, J6.pin2
  N9: PNP.B, R12.Pin_0
  N10: PNP_2.E, R10.Pin_0, J6.pin1
  N11: PNP_2.B, R13.Pin_0
  N12: IC2.pin1, R7.Pin_0, R8.Pin_1
  N13: IC2.pin2, R8.Pin_0, R9.Pin_0
  N14: IC2.pin4, J7.pin4, C2.1
  N15: IC2.pin5, R7.Pin_1
  N16: IC2.pin6, R5.Pin_0, R6.Pin_0
  N17: IC2.pin7, R2.Pin_0, R5.Pin_1
  N18: IC2.pin8, J7.pin3, C2.0
  N19: J3.pin1, R1.Pin_1
  N20: J3.pin2, R3.Pin_1
  N21: J3.pin4, R4.Pin_1
  N22: J3.pin5, R2.Pin_1
  N23: R12.Pin_1, J4.pin4
  N24: R13.Pin_1, J4.pin5
  N25: J4.pin1, J6.pin5
  N26: J4.pin2, J6.pin4
  N27: J4.pin3, J6.pin3
