# Fritzing sketch Simplex PCB front (saved by Fritzing 0.9.4)
circuit board: 2cm x 10cm
perfboards: 1

parts:
  10kΩ = Potentiometer
  10kΩ_2 = Potentiometer
  10kΩ_3 = Potentiometer
  3_5mm2 = 3.5mm verticle mono jack
  3_5mm4 = 3.5mm verticle mono jack
  LED = LED - 5mm [color="Red (633nm)" package="5 mm [THT]"]
  3_5mm1 = 3.5mm verticle mono jack
  LED_2 = LED - 5mm [color="Red (633nm)" package="5 mm [THT]"]
  3_5mm3 = 3.5mm verticle mono jack
  J1 = male pin header, 5 pins [form="♂ (male)"]
  J2 = male pin header, 5 pins [form="♂ (male)"]
  J9 = male pin header, 2 pins [form="♂ (male)"]

nets:
  GND: 10kΩ.CCW, 10kΩ.Chassis#3, 10kΩ_2.CCW, 10kΩ_2.Chassis#3, 10kΩ_3.CCW, 10kΩ_3.Chassis#3, 3_5mm2.Shank, 3_5mm2.Switch, 3_5mm4.Shank, 3_5mm4.Switch, LED.cathode, 3_5mm1.Shank, LED_2.cathode, 3_5mm3.Shank, J1.pin3, J9.pin2
  N1: 10kΩ.WIPER, J2.pin5
  N2: 10kΩ.CW, 10kΩ_2.CW, 10kΩ_3.CW, J9.pin1
  N3: 10kΩ_2.WIPER, J2.pin3
  N4: 10kΩ_3.WIPER, J2.pin4
  N5: 3_5mm2.Tip, J2.pin1
  N6: 3_5mm4.Tip, J2.pin2
  N7: LED.anode, J1.pin4
  N8: 3_5mm1.Tip, J1.pin1
  N9: LED_2.anode, J1.pin2
  N10: 3_5mm3.Tip, J1.pin5

custom parts:
  Potentiometer: Modular Addict 9mm vertical potentiometer
  3.5mm verticle mono jack: Thonkiconn pj301m-12 verticle mono switched 3.5mm jack.
