# Fritzing sketch Simplex PCB backpack (saved by Fritzing 0.9.4)
circuit board: 2cm x 10cm
perfboards: 1

parts:
  Arduino_Nano_3_0 = Arduino Nano (Rev3.0)
  -12v = shrouded pin header, 16 pins [form="♂ (shrouded male)"]
  J8 = male pin header, 3 pins [form="♂ (male)"]
  J9 = male pin header, 4 pins [form="♂ (male)"]
  J10 = male pin header, 5 pins [form="♂ (male)"]

nets:
  N1: Arduino_Nano_3_0.GND, -12v.pin2, -12v.pin3, -12v.pin4, -12v.pin13, -12v.pin14, -12v.pin15, J9.pin1
  N2: Arduino_Nano_3_0.D8, J8.pin3
  N3: Arduino_Nano_3_0.D11/MOSI, J8.pin2
  N4: Arduino_Nano_3_0.5V, -12v.pin5, -12v.pin12, J9.pin2
  N5: Arduino_Nano_3_0.A4, J10.pin1
  N6: Arduino_Nano_3_0.A3, J10.pin2
  N7: Arduino_Nano_3_0.A2, J10.pin3
  N8: Arduino_Nano_3_0.A1, J10.pin4
  N9: Arduino_Nano_3_0.A0, J10.pin5
  N10: Arduino_Nano_3_0.D13/SCK, J8.pin1
  N11: -12v.pin1, -12v.pin16, J9.pin4
  N12: -12v.pin6, -12v.pin11, J9.pin3
