# Fritzing sketch clock_front_pcb (saved by Fritzing 0.9.4)
circuit board: 3.9cm x 10cm
perfboards: 1

parts:
  R1 = Resistor [tolerance=±5% resistance=1k package=THT]
  R9 = Resistor [tolerance=±5% resistance=220 package=THT]
  LED2 = LED - 5mm [color="Red (633nm)" package="5 mm [THT]"]
  R2 = Resistor [tolerance=±5% resistance=1k package=THT]
  R10 = Resistor [tolerance=±5% resistance=220 package=THT]
  LED3 = LED - 5mm [color="Red (633nm)" package="5 mm [THT]"]
  R3 = Resistor [tolerance=±5% resistance=1k package=THT]
  R12 = Resistor [tolerance=±5% resistance=220 package=THT]
  R11 = Resistor [tolerance=±5% resistance=220 package=THT]
  R4 = Resistor [tolerance=±5% resistance=1k package=THT]
  LED4 = LED - 5mm [color="Red (633nm)" package="5 mm [THT]"]
  LED5 = LED - 5mm [color="Red (633nm)" package="5 mm [THT]"]
  R5 = Resistor [tolerance=±5% resistance=1k package=THT]
  R14 = Resistor [tolerance=±5% resistance=220 package=THT]
  R13 = Resistor [tolerance=±5% resistance=220 package=THT]
  R6 = Resistor [tolerance=±5% resistance=1k package=THT]
  LED6 = LED - 5mm [color="Red (633nm)" package="5 mm [THT]"]
  LED7 = LED - 5mm [color="Red (633nm)" package="5 mm [THT]"]
  R7 = Resistor [tolerance=±5% resistance=1k package=THT]
  R16 = Resistor [tolerance=±5% resistance=220 package=THT]
  R15 = Resistor [tolerance=±5% resistance=220 package=THT]
  R8 = Resistor [tolerance=±5% resistance=1k package=THT]
  LED8 = LED - 5mm [color="Red (633nm)" package="5 mm [THT]"]
  LED9 = LED - 5mm [color="Red (633nm)" package="5 mm [THT]"]
  Encoder1 = Rotary encoder with push button
  OLED_I2C1 = OLED 128x64 I2C Monochrome Display
  3_5mm6 = 3.5mm verticle mono jack
  3_5mm2 = 3.5mm verticle mono jack
  3_5mm8 = 3.5mm verticle mono jack
  3_5mm5 = 3.5mm verticle mono jack
  3_5mm3 = 3.5mm verticle mono jack
  3_5mm1 = 3.5mm verticle mono jack
  3_5mm7 = 3.5mm verticle mono jack
  3_5mm4 = 3.5mm verticle mono jack
  J2 = male pin header, 4 pins [form="♂ (male)"]
  J3 = male pin header, 7 pins [form="♂ (male)"]
  J1 = male pin header, 4 pins [form="♂ (male)"]

nets:
  N1: R1.Pin_0, 3_5mm1.Tip
  N2: R1.Pin_1, R9.Pin_0, J1.pin4
  N3: R9.Pin_1, LED2.anode
  N4: LED2.cathode, LED3.cathode, LED4.cathode, LED5.cathode, LED6.cathode, LED7.cathode, LED8.cathode, LED9.cathode, Encoder1.COM, Encoder1.SPST1A, OLED_I2C1.GND, 3_5mm6.Shank, 3_5mm2.Shank, 3_5mm8.Shank, 3_5mm5.Shank, 3_5mm3.Shank, 3_5mm1.Shank, 3_5mm7.Shank, 3_5mm4.Shank, J3.pin6
  N5: R2.Pin_0, 3_5mm2.Tip
  N6: R2.Pin_1, R10.Pin_0, J2.pin4
  N7: R10.Pin_1, LED3.anode
  N8: R3.Pin_0, 3_5mm3.Tip
  N9: R3.Pin_1, R11.Pin_0, J1.pin3
  N10: R12.Pin_0, R4.Pin_1, J2.pin3
  N11: R12.Pin_1, LED5.anode
  N12: R11.Pin_1, LED4.anode
  N13: R4.Pin_0, 3_5mm4.Tip
  N14: R5.Pin_0, 3_5mm5.Tip
  N15: R5.Pin_1, R13.Pin_0, J1.pin2
  N16: R14.Pin_0, R6.Pin_1, J2.pin2
  N17: R14.Pin_1, LED7.anode
  N18: R13.Pin_1, LED6.anode
  N19: R6.Pin_0, 3_5mm6.Tip
  N20: R7.Pin_0, 3_5mm7.Tip
  N21: R7.Pin_1, R15.Pin_0, J1.pin1
  N22: R16.Pin_0, R8.Pin_1, J2.pin1
  N23: R16.Pin_1, LED9.anode
  N24: R15.Pin_1, LED8.anode
  N25: R8.Pin_0, 3_5mm8.Tip
  N26: Encoder1.Encoder_A, J3.pin7
  N27: Encoder1.Encoder_B, J3.pin5
  N28: Encoder1.SPST1B, J3.pin4
  N29: OLED_I2C1.SDA, J3.pin1
  N30: OLED_I2C1.SCK, J3.pin2
  N31: OLED_I2C1.VDD, J3.pin3

notes:
  Clock front v1.0
  I2C
  Screen
  encoder

custom parts:
  3.5mm verticle mono jack: Thonkiconn pj301m-12 verticle mono switched 3.5mm jack.
