# Fritzing sketch mixer_pcb (saved by Fritzing 0.9.4)
circuit board: 4cm x 10cm
perfboards: 1

parts:
  J1 = shrouded pin header, 10 pins [form="♂ (shrouded male)"]
  B100k = Potentiometer
  B100k_2 = Potentiometer
  B100k_3 = Potentiometer
  B100k_4 = Potentiometer
  3_5mm2 = 3.5mm verticle mono jack
  3_5mm1 = 3.5mm verticle mono jack
  3_5mm3 = 3.5mm verticle mono jack
  3_5mm4 = 3.5mm verticle mono jack
  3_5mm5 = 3.5mm verticle mono jack
  3_5mm6 = 3.5mm verticle mono jack
  LED = LED - 3mm [color="Red (633nm)" package="3 mm [THT]"]
  IC1 = IC, DIP package, 8 pins [chip_label=TL072]
  C1 = Electrolytic Capacitor [capacitance=10µF package="100 mil [THT, electrolytic]"]
  C2 = Electrolytic Capacitor [capacitance=10µF package="100 mil [THT, electrolytic]"]
  C3 = Ceramic Capacitor [capacitance=100nF package="100 mil [THT, multilayer]"]
  C4 = Ceramic Capacitor [capacitance=100nF package="100 mil [THT, multilayer]"]
  chain_in = female pin header, 2 pins [form="♀ (female)"]
  chain_out = female pin header, 2 pins [form="♀ (female)"]
  R13 = Resistor [tolerance=±5% resistance=1k package=THT]
  R12 = Resistor [tolerance=±5% resistance=100k package=THT]
  R11 = Resistor [tolerance=±5% resistance=100k package=THT]
  R10 = Resistor [tolerance=±5% resistance=100k package=THT]
  R15 = Resistor [tolerance=±5% resistance=100k package=THT]
  R9 = Resistor [tolerance=±5% resistance=100k package=THT]
  R8 = Resistor [tolerance=±5% resistance=100k package=THT]
  R7 = Resistor [tolerance=±5% resistance=100k package=THT]
  R6 = Resistor [tolerance=±5% resistance=100k package=THT]
  R5 = Resistor [tolerance=±5% resistance=100k package=THT]
  R16 = Resistor [tolerance=±5% resistance=470 package=THT]
  S6 = Toggle Switch [package=THT]
  S7 = Toggle Switch [package=THT]
  S8 = Toggle Switch [package=THT]
  S9 = Toggle Switch [package=THT]
  S10 = Toggle Switch [package=THT]

nets:
  N1: J1.pin1, J1.pin10, IC1.pin4, C2.-, C3.0
  N2: J1.pin2, J1.pin3, J1.pin4, J1.pin7, J1.pin8, J1.pin9, B100k.CCW, B100k.Chassis#4, B100k_2.CCW, B100k_2.Chassis, B100k_3.CCW, B100k_3.Chassis, B100k_4.CCW, B100k_4.Chassis#3, 3_5mm2.Shank, 3_5mm2.Switch, 3_5mm1.Shank, 3_5mm1.Switch, 3_5mm3.Shank, 3_5mm4.Shank, 3_5mm4.Switch, 3_5mm5.Shank, 3_5mm5.Switch, 3_5mm6.Shank, LED.anode, IC1.pin3, IC1.pin5, C1.-, C2.+, C3.1, C4.1, chain_in.pin1, chain_out.pin1, S6.L1, S7.L1, S8.L1, S9.L1, S10.L1
  N3: J1.pin5, J1.pin6, IC1.pin8, C1.+, C4.0
  N4: B100k.WIPER, R5.Pin_0
  N5: B100k.CW, S6.COM
  N6: B100k_2.WIPER, R6.Pin_0
  N7: B100k_2.CW, S8.COM
  N8: B100k_3.WIPER, R7.Pin_0
  N9: B100k_3.CW, S7.COM
  N10: B100k_4.WIPER, R8.Pin_0
  N11: B100k_4.CW, S9.COM
  N12: 3_5mm2.Tip, S8.L2
  N13: 3_5mm1.Tip, S6.L2
  N14: 3_5mm3.Tip, S7.L2
  N15: 3_5mm4.Tip, S9.L2
  N16: 3_5mm5.Tip, S10.L2
  N17: 3_5mm6.Switch, chain_out.pin2
  N18: 3_5mm6.Tip, R13.Pin_1
  N19: LED.cathode, R16.Pin_0
  N20: IC1.pin1, R11.Pin_0, R10.Pin_1, R16.Pin_1
  N21: IC1.pin2, R10.Pin_0, R15.Pin_1, R9.Pin_1, R8.Pin_1, R7.Pin_1, R6.Pin_1, R5.Pin_1
  N22: IC1.pin6, R12.Pin_1, R11.Pin_1
  N23: IC1.pin7, R13.Pin_0, R12.Pin_0
  N24: chain_in.pin2, R15.Pin_0
  N25: R9.Pin_0, S10.COM

notes:
  -12v
  Mixer v0.3
  -

custom parts:
  Potentiometer: Modular Addict 9mm vertical potentiometer
  3.5mm verticle mono jack: Thonkiconn pj301m-12 verticle mono switched 3.5mm jack.
