# Fritzing sketch oa_back (saved by Fritzing 0.9.4)
circuit board: 2cm x 10cm
perfboards: 1

parts:
  R1 = Resistor [tolerance=±5% resistance=10k package=THT]
  IC1 = IC, DIP package, 14 pins [chip_label=TL074]
  R2 = Resistor [tolerance=±5% resistance=10k package=THT]
  R4 = Resistor [tolerance=±5% resistance=10k package=THT]
  R5 = Resistor [tolerance=±5% resistance=10k package=THT]
  R6 = Resistor [tolerance=±5% resistance=10k package=THT]
  J1 = male pin header, 7 pins [form="♂ (male)"]
  J2 = male pin header, 7 pins [form="♂ (male)"]
  R7 = Resistor [tolerance=±5% resistance=10k package=THT]
  R8 = Resistor [tolerance=±5% resistance=10k package=THT]
  R9 = Resistor [tolerance=±5% resistance=10k package=THT]
  R10 = Resistor [tolerance=±5% resistance=10k package=THT]
  R11 = Resistor [tolerance=±5% resistance=10k package=THT]
  J3 = shrouded pin header, 10 pins [form="♂ (shrouded male)"]
  C1 = Ceramic Capacitor [capacitance=100nF package="100 mil [THT, multilayer]"]
  C3 = Electrolytic Capacitor [capacitance=10µF package="100 mil [THT, electrolytic]"]
  C4 = Electrolytic Capacitor [capacitance=10µF package="100 mil [THT, electrolytic]"]

nets:
  N1: R1.Pin_0, J1.pin4
  N2: R1.Pin_1, IC1.pin9, R5.Pin_0, R6.Pin_0
  N3: IC1.pin1, R9.Pin_1, R11.Pin_0
  N4: IC1.pin2, R10.Pin_0, R11.Pin_1
  N5: IC1.pin3, J2.pin3
  N6: IC1.pin4, J1.pin7, J2.pin7, J3.pin5, J3.pin6, C1.0, C4.+
  N7: IC1.pin5, IC1.pin10, J1.pin5, J2.pin5, J3.pin2, J3.pin3, J3.pin4, J3.pin7, J3.pin8, J3.pin9, C3.+, C4.-
  N8: IC1.pin6, R7.Pin_0, R8.Pin_1, R9.Pin_0
  N9: IC1.pin7, J2.pin1, R7.Pin_1
  N10: IC1.pin8, R6.Pin_1, J1.pin1
  N11: IC1.pin11, J1.pin6, J2.pin6, J3.pin1, J3.pin10, C1.1, C3.-
  N12: IC1.pin12, J1.pin3
  N13: IC1.pin13, R2.Pin_0, R4.Pin_1
  N14: IC1.pin14, R2.Pin_1, R5.Pin_1
  N15: R4.Pin_0, J1.pin2
  N16: J2.pin2, R10.Pin_1
  N17: J2.pin4, R8.Pin_0

notes:
  -12v
  O/A back
  v0.2
