# Fritzing sketch quantizer_back (saved by Fritzing 0.9.4)
circuit board: 4cm x 10cm
stripboards: 1

parts:
  Arduino_Nano_v3_0 = Arduino Nano (Rev3.0)
  IC1 = IC, DIP package, 8 pins [chip_label=TL072]
  R5 = Resistor [tolerance=±5% resistance=20k package=THT]
  R6 = Resistor [tolerance=±5% resistance=20k package=THT]
  R7 = Resistor [tolerance=±5% resistance=10k package=THT]
  R8 = Resistor [tolerance=±5% resistance=10k package=THT]
  IC2 = IC, DIP package, 28 pins [chip_label=TLC5940NT]
  R15 = Resistor [tolerance=±5% resistance=2k package=THT]
  IC3 = IC, DIP package, 14 pins [chip_label=TL074]
  IC4 = IC, DIP package, 14 pins [chip_label=MCP4922]
  R16 = Resistor [tolerance=±5% resistance=10k package=THT]
  R17 = Resistor [tolerance=±5% resistance=10k package=THT]
  R18 = Resistor [tolerance=±5% resistance=10k package=THT]
  R19 = Resistor [tolerance=±5% resistance=10k package=THT]
  R20 = Resistor [tolerance=±5% resistance=10k package=THT]
  R21 = Resistor [tolerance=±5% resistance=10k package=THT]
  R22 = Resistor [tolerance=±5% resistance=10k package=THT]
  R23 = Resistor [tolerance=±5% resistance=10k package=THT]
  R24 = Resistor [tolerance=±5% resistance=10k package=THT]
  R25 = Resistor [tolerance=±5% resistance=10k package=THT]
  J1 = shrouded pin header, 16 pins [form="♂ (shrouded male)"]
  PNP = PNP-Transistor [package="TO92 [THT]"]
  R26 = Resistor [tolerance=±5% resistance=100k package=THT]
  R27 = Resistor [tolerance=±5% resistance=1k package=THT]
  PNP_2 = PNP-Transistor [package="TO92 [THT]"]
  R28 = Resistor [tolerance=±5% resistance=100k package=THT]
  R29 = Resistor [tolerance=±5% resistance=1k package=THT]
  J6 = female pin header, 2 pins [form="♀ (female)"]
  J4 = female pin header, 12 pins [form="♀ (female)"]
  J3 = female pin header, 2 pins [form="♀ (female)"]
  J2 = female pin header, 2 pins [form="♀ (female)"]
  J5 = female pin header, 4 pins [form="♀ (female)"]
  R30 = Resistor [tolerance=±5% resistance=100k package=THT]
  R31 = Resistor [tolerance=±5% resistance=100k package=THT]
  R3 = Resistor [tolerance=±5% resistance=20k package=THT]
  R4 = Resistor [tolerance=±5% resistance=20k package=THT]
  C1 = Ceramic Capacitor [capacitance=100nF package="100 mil [THT, multilayer]"]
  C2 = Ceramic Capacitor [capacitance=100nF package="100 mil [THT, multilayer]"]
  Expander = female pin header, 5 pins [form="♀ (female)"]
  C4 = Electrolytic Capacitor [capacitance=10µF package="100 mil [THT, electrolytic]"]
  C3 = Ceramic Capacitor [capacitance=100nF package="100 mil [THT, multilayer]"]

nets:
  N1: Arduino_Nano_v3_0.GND, R5.Pin_1, R6.Pin_0, IC2.pin19, IC2.pin22, IC2.pin27, R15.Pin_1, IC4.pin8, IC4.pin12, R20.Pin_0, R25.Pin_0, J1.pin2, J1.pin3, J1.pin4, J1.pin13, J1.pin14, J1.pin15, PNP.C, PNP_2.C, J5.pin2, C4.-, C3.0
  N2: Arduino_Nano_v3_0.D2, J6.pin1
  N3: Arduino_Nano_v3_0.D3, IC2.pin18
  N4: Arduino_Nano_v3_0.D4, R29.Pin_1
  N5: Arduino_Nano_v3_0.D5, R27.Pin_0
  N6: Arduino_Nano_v3_0.D8, IC4.pin3
  N7: Arduino_Nano_v3_0.D9, IC2.pin24
  N8: Arduino_Nano_v3_0.D10, IC2.pin23
  N9: Arduino_Nano_v3_0.D11/MOSI, IC2.pin26, IC4.pin5
  N10: Arduino_Nano_v3_0.5V, R7.Pin_1, R8.Pin_1, IC2.pin21, IC4.pin1, IC4.pin9, IC4.pin11, IC4.pin13, R16.Pin_1, R23.Pin_1, J1.pin6, J1.pin11, J5.pin3, R30.Pin_0, R31.Pin_0, C4.+, C3.1
  N11: Arduino_Nano_v3_0.A7, R6.Pin_1, R8.Pin_0, R3.Pin_0
  N12: Arduino_Nano_v3_0.A6, R5.Pin_0, R7.Pin_0, R4.Pin_0
  N13: Arduino_Nano_v3_0.A5, Expander.pin1
  N14: Arduino_Nano_v3_0.A4, Expander.pin2
  N15: Arduino_Nano_v3_0.A3, Expander.pin3
  N16: Arduino_Nano_v3_0.A2, Expander.pin4
  N17: Arduino_Nano_v3_0.A1, Expander.pin5
  N18: Arduino_Nano_v3_0.A0, J6.pin2
  N19: Arduino_Nano_v3_0.D13/SCK, IC2.pin25, IC4.pin4
  N20: IC1.pin1, IC1.pin2, R4.Pin_1
  N21: IC1.pin3, J2.pin2
  N22: IC1.pin4, IC3.pin11, J1.pin1, J1.pin16, C1.0, C2.0
  N23: IC1.pin5, J2.pin1
  N24: IC1.pin6, IC1.pin7, R3.Pin_1
  N25: IC1.pin8, IC3.pin4, J1.pin5, J1.pin12, C1.1, C2.1
  N26: IC2.pin1, J4.pin12
  N27: IC2.pin2, J4.pin11
  N28: IC2.pin3, J4.pin10
  N29: IC2.pin4, J4.pin9
  N30: IC2.pin5, J4.pin8
  N31: IC2.pin6, J4.pin7
  N32: IC2.pin7, J4.pin6
  N33: IC2.pin8, J4.pin5
  N34: IC2.pin9, J4.pin4
  N35: IC2.pin10, J4.pin3
  N36: IC2.pin11, J4.pin2
  N37: IC2.pin12, J4.pin1
  N38: IC2.pin20, R15.Pin_0
  N39: IC3.pin1, R21.Pin_1, R22.Pin_1
  N40: IC3.pin2, R22.Pin_0, R23.Pin_0
  N41: IC3.pin3, IC4.pin14
  N42: IC3.pin5, R21.Pin_0
  N43: IC3.pin6, R24.Pin_1, R25.Pin_1
  N44: IC3.pin7, R24.Pin_0, J3.pin1
  N45: IC3.pin8, R19.Pin_0, J3.pin2
  N46: IC3.pin9, R19.Pin_1, R20.Pin_1
  N47: IC3.pin10, R18.Pin_0
  N48: IC3.pin12, IC4.pin10
  N49: IC3.pin13, R16.Pin_0, R17.Pin_0
  N50: IC3.pin14, R17.Pin_1, R18.Pin_1
  N51: PNP.E, R27.Pin_1, R31.Pin_1
  N52: PNP.B, R26.Pin_0
  N53: R26.Pin_1, J5.pin4
  N54: PNP_2.E, R29.Pin_0, R30.Pin_1
  N55: PNP_2.B, R28.Pin_1
  N56: R28.Pin_0, J5.pin1

notes:
  -12v
  Quantizer back v0.2
