# Fritzing sketch quantizer_front (saved by Fritzing 0.9.4)
circuit board: 2.85cm x 10cm
perfboards: 1

parts:
  3_5mm1 = 3.5mm verticle mono jack
  3_5mm2 = 3.5mm verticle mono jack
  3_5mm4 = 3.5mm verticle mono jack
  3_5mm5 = 3.5mm verticle mono jack
  3_5mm6 = 3.5mm verticle mono jack
  3_5mm7 = 3.5mm verticle mono jack
  J5 = female pin header, 12 pins [form="♀ (female)"]
  J6 = female pin header, 2 pins [form="♀ (female)"]
  J7 = female pin header, 2 pins [form="♀ (female)"]
  J9 = male pin header, 3 pins [form="♂ (male)"]
  J10 = male pin header, 3 pins [form="♂ (male)"]
  J11 = male pin header, 3 pins [form="♂ (male)"]
  J12 = male pin header, 3 pins [form="♂ (male)"]
  J13 = male pin header, 3 pins [form="♂ (male)"]
  J14 = male pin header, 3 pins [form="♂ (male)"]
  J15 = male pin header, 3 pins [form="♂ (male)"]
  J16 = male pin header, 3 pins [form="♂ (male)"]
  J17 = male pin header, 3 pins [form="♂ (male)"]
  J18 = male pin header, 3 pins [form="♂ (male)"]
  J19 = male pin header, 3 pins [form="♂ (male)"]
  J20 = male pin header, 3 pins [form="♂ (male)"]
  Button = male pin header, 2 pins [form="♂ (male)"]
  R13 = Resistor [tolerance=±5% resistance=1k package=THT]
  R14 = Resistor [tolerance=±5% resistance=1k package=THT]
  R15 = Resistor [tolerance=±5% resistance=1k package=THT]
  R16 = Resistor [tolerance=±5% resistance=1k package=THT]
  R17 = Resistor [tolerance=±5% resistance=1k package=THT]
  R18 = Resistor [tolerance=±5% resistance=1k package=THT]
  R19 = Resistor [tolerance=±5% resistance=1k package=THT]
  R20 = Resistor [tolerance=±5% resistance=1k package=THT]
  R21 = Resistor [tolerance=±5% resistance=1k package=THT]
  R22 = Resistor [tolerance=±5% resistance=1k package=THT]
  R23 = Resistor [tolerance=±5% resistance=1k package=THT]
  R24 = Resistor [tolerance=±5% resistance=1k package=THT]
  GND = female pin header, 1 pin [form="♀ (female)"]
  J22 = female pin header, 4 pins [form="♀ (female)"]
  J1 = female pin header, 2 pins [form="♀ (female)"]

nets:
  N1: 3_5mm1.Shank, 3_5mm1.Switch, 3_5mm2.Shank, 3_5mm4.Shank, 3_5mm5.Shank, 3_5mm6.Shank, 3_5mm6.Switch, 3_5mm7.Shank, 3_5mm7.Switch, Button.pin1, R24.Pin_1, GND.pin1, J22.pin2
  N2: 3_5mm1.Tip, J7.pin2
  N3: 3_5mm2.Tip, J22.pin1
  N4: 3_5mm4.Tip, J6.pin2
  N5: 3_5mm5.Tip, J22.pin4
  N6: 3_5mm6.Tip, J7.pin1
  N7: 3_5mm7.Tip, J6.pin1
  N8: J5.pin1, J9.pin2
  N9: J5.pin2, J10.pin2
  N10: J5.pin3, J11.pin2
  N11: J5.pin4, J12.pin2
  N12: J5.pin5, J13.pin2
  N13: J5.pin6, J14.pin2
  N14: J5.pin7, J19.pin2
  N15: J5.pin8, J16.pin2
  N16: J5.pin9, J20.pin2
  N17: J5.pin10, J18.pin2
  N18: J5.pin11, J15.pin2
  N19: J5.pin12, J17.pin2
  N20: J9.pin1, R22.Pin_1, R24.Pin_0, J1.pin1
  N21: J9.pin3, J10.pin3, J11.pin3, J12.pin3, J13.pin3, J14.pin3, J15.pin3, J16.pin3, J17.pin3, J18.pin3, J19.pin3, J20.pin3, J22.pin3
  N22: J10.pin1, R21.Pin_1, R22.Pin_0
  N23: J11.pin1, R21.Pin_0, R23.Pin_1
  N24: J12.pin1, R20.Pin_1, R23.Pin_0
  N25: J13.pin1, R18.Pin_1, R20.Pin_0
  N26: J14.pin1, R17.Pin_1, R18.Pin_0
  N27: J15.pin1, R13.Pin_1, R15.Pin_0
  N28: J16.pin1, R16.Pin_1, R19.Pin_0
  N29: J17.pin1, R13.Pin_0
  N30: J18.pin1, R14.Pin_0, R15.Pin_1
  N31: J19.pin1, R17.Pin_0, R19.Pin_1
  N32: J20.pin1, R14.Pin_1, R16.Pin_0
  N33: Button.pin2, J1.pin2

notes:
  GND
  5v
  LED
  BUTTON
  Quantizer front v0.2

custom parts:
  3.5mm verticle mono jack: Thonkiconn pj301m-12 verticle mono switched 3.5mm jack.
